# Fritzing sketch Untitled Sketch (saved by Fritzing 0.9.3b)
breadboards: 1

parts:
  WeMos_D1_Mini1 = WeMos D1 Mini
  LED1 = LED - 5mm [color="Red (633nm)" package="5 mm [THT]"]

nets:
  N1: WeMos_D1_Mini1.D4, LED1.anode
  N2: WeMos_D1_Mini1.G, LED1.cathode

// code stored in the sketch: Untitled.ino
/*New blynk app project
 * https://srituhobby.com
 */
 
#define BLYNK_PRINT Serial
#define BLYNK_TEMPLATE_ID "TMPLXOcrVkgE"
#define BLYNK_DEVICE_NAME "Lampu"
#define BLYNK_AUTH_TOKEN "fifzZWeizjnQyWw6br7S7YhJagnL4Mll"

#include <ESP8266WiFi.h>
#include <BlynkSimpleEsp8266.h>

char auth[] = BLYNK_AUTH_TOKEN;
char ssid[] = "Flowers_bouquet04";//Enter your WIFI name
char pass[] = "tazus010402";//Enter your WIFI password


BLYNK_WRITE(V0) {
  digitalWrite(D4, param.asInt());
}

void setup() {
  pinMode(D4, OUTPUT);
  Blynk.begin(auth, ssid, pass, "blynk.cloud", 80);
}

void loop() {
  Blynk.run();
}
